# Fritzing sketch esp32-ButtonPot (saved by Fritzing 0.9.4)
breadboards: 1

parts:
  Part1 = Adafruit HUZZAH32 ESP32 Feather [part_number="Adafruit #3405"]
  S1 = Momentary Switch [package=ksa_sealed_tac_switch]
  R3 = Resistor [tolerance=±5% resistance=10k package="0805 [SMD]"]
  R4 = Resistor [tolerance=±5% resistance=1k package="0805 [SMD]"]
  R5 = Rotary Potentiometer (Small) [maximum_resistance=100kΩ package=THT]

nets:
  N1: Part1.SCK, S1.2, R3.Pin_0
  N2: Part1.A2_I34, R5.wiper
  N3: Part1.GND, R3.Pin_1, R5.leg2
  N4: Part1.3.3V, R4.Pin_0, R5.leg1
  N5: S1.3, R4.Pin_1
